// Logisim project Examplequiz.circ as structural Verilog: 1 circuit, main circuit main
module main (
  input  A,
  input  B,
  input  C,
  output D
);

  nor nor_1 (D, A, B, C);

  // Notes on the sheet:
  //   1. Om A=1, B=1, C=0,Vad är D?
  //   2. Om A=1, B=unknown, C=0, Vad är D?
endmodule
